# Fritzing sketch sdadasfyrkjyfudhnj (saved by Fritzing 0.9.3b)
breadboards: 1

parts:
  Parça1 = Arduino Nano (Rev3.0)
  L298N1 = L298N DC motor driver
  Parça2 = Bluetooth HC-05 Macho
  J1 = Piezo Speaker
  LED1 = LED - 5mm [color="Red (633nm)" package="5 mm [THT]"]
  LED2 = LED - 5mm [color="Red (633nm)" package="5 mm [THT]"]
  LED3 = LED - 5mm [color="Red (633nm)" package="5 mm [THT]"]
  LED4 = LED - 5mm [color="Red (633nm)" package="5 mm [THT]"]
  R1 = Photocell (LDR) [package=THT]  # not connected
  R2 = Resistor [tolerance=±5% resistance=10 package=THT]  # not connected

nets:
  N1: Parça1.D2, LED1.anode
  N2: Parça1.D3, J1.pin2
  N3: Parça1.D4, Parça2.State
  N4: Parça1.D5, Parça1.D6, Parça1.D7, Parça1.D8, Parça1.D9, Parça1.D10, L298N1.ENA, L298N1.ENB, L298N1.IN1, L298N1.IN2, L298N1.IN3, L298N1.IN4
  N5: Parça1.D11/MOSI, Parça2.TXD
  N6: Parça1.D12/MISO, Parça2.RXD
  N7: Parça1.D13/SCK, LED4.anode
  N8: L298N1.5V, LED2.cathode, LED3.cathode
  N9: LED1.cathode, LED2.anode
  N10: LED3.anode, LED4.cathode

custom parts:
  L298N DC motor driver: 2x DC motor driver with 78M05 positive voltage regulator (7..35 V) L298N: max 46 V, 2 A Set 5 V Enable jumper to enable 5 V regultor (needed for the L298N) and +5 V output at screw terminal or supply external +5 V at screw terminal Set ENA and/or ENB to +5 V to enable motor permanently or supply ENA and/or ENB with PWM signal IN1 and IN2 set rotation directory for motor A (OUT1/OUT2) IN2 and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
